// Logisim project _main.circ as structural Verilog: 2 circuits, main circuit main
module main (
);

  wire and_1_out, button_1_out, clock_1_out, clock_2_out, clock_3_out, DECODE_ENABLE, EXECUTE_ENABLE,
       FETCH_ENABLE, MEMORY_ENABLE, not_1_out, RAM_STORE_ENABLE, WRITEBACK_ENABLE;
  wire [2:0] counter_1_q;
  wire [7:0] adder_1_out, RAM_ADDR, rom_loader_1_p2;
  wire [31:0] RAM_DATA_IN, RAM_DATA_OUT, rom_loader_1_p3;

  and and_1 (and_1_out, clock_1_out, not_1_out);
  Clock clock_1 (.out(clock_1_out));
  Button button_1 (.out(button_1_out));
  Counter #(.width(3), .max('h4)) counter_1 (.Q(counter_1_q), .clk(and_1_out));  // open: load, D, count, carry, clr
  Decoder #(.select(3), .disabled(0)) decoder_1 (
    .out0(FETCH_ENABLE), .out1(DECODE_ENABLE), .out2(EXECUTE_ENABLE), .out3(MEMORY_ENABLE),
    .out4(WRITEBACK_ENABLE), .sel(counter_1_q), .en(not_1_out));  // open: out5, out6, out7
  not not_1 (not_1_out, RAM_STORE_ENABLE);
  // ROM_loader rom_loader_1: pin names not known; wires that end beside it: button_1_out, rom_loader_1_p2, rom_loader_1_p3, RAM_STORE_ENABLE
  // Probe on RAM_ADDR
  // Probe on RAM_DATA_IN
  Register register_1 (.en(FETCH_ENABLE), .Q(RAM_ADDR), .clk(clock_2_out));  // open: D, clr
  Clock clock_2 (.out(clock_2_out));
  assign RAM_ADDR = RAM_STORE_ENABLE ? rom_loader_1_p2 : 8'bz;  // Controlled_Buffer controlled_buffer_1
  assign RAM_DATA_IN = RAM_STORE_ENABLE ? rom_loader_1_p3 : 32'bz;  // Controlled_Buffer controlled_buffer_2
  // ALU alu_1: pin names not known
  Adder adder_1 (.a(RAM_ADDR), .b(8'h1), .out(adder_1_out));  // open: cin, cout
  // _6x8_Register_File 6x8_register_file_1: pin names not known
  Clock clock_3 (.out(clock_3_out));
  RAM #(.dataWidth(32), .bus("separate")) ram_1 (
    .addr(RAM_ADDR), .din(RAM_DATA_IN), .data(RAM_DATA_OUT), .str(RAM_STORE_ENABLE), .clk(clock_3_out),
    .ld(FETCH_ENABLE));  // open: sel, clr

  // Other names for the same wires on the sheet: RAM_LOAD_ENABLE = FETCH_ENABLE

  // Notes on the sheet:
  //   ioeajsrjeaior
endmodule

module instruction_memory (
  input  ENABLE,
  output [3:0] ICODE,
  output [3:0] IFUN,
  output [3:0] rA,
  output [3:0] rB,
  output [15:0] valC,
  output [7:0] PC
);

  wire clock_1_out;

  Register register_1 (.en(ENABLE), .Q(PC), .clk(clock_1_out));  // open: D, clr
  Clock clock_1 (.out(clock_1_out));

  // Other names for the same wires on the sheet: RAM_ADDR[7:0] = PC; RAM_DATA_OUT[31:0] = {valC, rB, rA, IFUN, ICODE};
  //   RAM_LOAD_ENABLE = ENABLE

  // Notes on the sheet:
  //   ENABLE: pull=down
endmodule
